# Fritzing sketch halloween-doorway (saved by Fritzing 0.9.3b)

parts:
  U1 = NodeMCU V1.0
  Part1 = Adafruit VL53L0X Time of Flight Distance Sensor [part_number="Adafruit #3317"]
  OLED_I2C1 = OLED 128x64 I2C Monochrome Display

nets:
  N1: U1.D1, Part1.SCL, OLED_I2C1.SCK
  N2: U1.D2, Part1.SDA, OLED_I2C1.SDA
  3V3: U1.3V3, Part1.VIN, OLED_I2C1.VDD
  GND: U1.GND, Part1.GND, OLED_I2C1.GND

custom parts:
  NodeMCU V1.0: ESP8266 based NodeMCU
  Adafruit VL53L0X Time of Flight Distance Sensor: The VL53L0X is a Time of Flight distance sensor like no other you've used! The sensor contains a very tiny invisible laser source, and a matching sensor. The VL53L0X can detect the "time of flight", or how long the light has taken to bounce back to the sensor. Since it uses a very narrow light source, it is good for determining distance of only the surface directly in front of it. Unlike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
